# Fritzing sketch shepherd-circuit-diagram (saved by Fritzing 0.8.6b)
breadboards: 1

parts:
  L3 = Solenoid
  Part1 = Arduino Uno (Rev3)
  R1 = Photocell (LDR) [package=THT]
  R2 = Resistor [tolerance=±5% resistance=1k package=THT]
  R4 = Resistor [tolerance=±5% resistance=1k package=THT]
  R6 = Resistor [tolerance=±5% resistance=1k package=THT]
  R7 = Photocell (LDR) [package=THT]
  R8 = Photocell (LDR) [package=THT]
  R9 = Photocell (LDR) [package=THT]
  R10 = Resistor [tolerance=±5% resistance=1k package=THT]
  Q1 = npn-Powertransistor [package="TO220 [THT]"]
  Q2 = npn-Powertransistor [package="TO220 [THT]"]
  Q3 = npn-Powertransistor [package="TO220 [THT]"]
  R11 = Resistor [tolerance=±5% resistance=220 package=THT]
  R12 = Resistor [tolerance=±5% resistance=220 package=THT]
  R13 = Resistor [tolerance=±5% resistance=220 package=THT]
  D3 = Diode [package=diode-1n4148]
  D4 = Diode [package=diode-1n4148]
  D5 = Diode [package=diode-1n4148]
  L5 = Solenoid
  Power_plug1 = Power plug
  L6 = Solenoid

nets:
  N1: L3.pin1, Q2.collector
  N2: L3.pin2, D3.A, D4.A, D5.A, L5.pin2, Power_plug1.GND, L6.pin2
  N3: Part1.A0, R1.pin_0, R2.Pin_0
  N4: Part1.A1, R4.Pin_0, R8.pin_0
  N5: Part1.A2, R6.Pin_0, R7.pin_0
  N6: Part1.A3, R9.pin_0, R10.Pin_0
  N7: Part1.D8, R13.Pin_0
  N8: Part1.D9_PWM, R12.Pin_0
  N9: Part1.D10_PWM/SS, R11.Pin_0
  N10: Part1.5V, R2.Pin_1, R4.Pin_1, R10.Pin_1
  N11: Part1.GND, R1.pin_1, R6.Pin_1, R7.pin_1, R8.pin_1, R9.pin_1
  N12: Q1.base, R11.Pin_1
  N13: Q1.collector, L5.pin1
  N14: Q1.emitter, Q2.emitter, Q3.emitter, Power_plug1.VCC
  N15: Q2.base, R12.Pin_1
  N16: Q3.base, R13.Pin_1
  N17: Q3.collector, L6.pin1
